// Digital circuit Assignment1.dig as structural Verilog
module Assignment1 (
  input  Clock,
  input  Reset,
  output [7:0] DataBus,
  output [4:0] AddressBus,
  output [2:0] Opcode,
  output Z
);

  wire and_1_out, controlssignalslogic_1_calu, controlssignalslogic_1_cd0, controlssignalslogic_1_cir,
       controlssignalslogic_1_cmar, controlssignalslogic_1_cmbr, controlssignalslogic_1_cpc,
       controlssignalslogic_1_ealu, controlssignalslogic_1_ed0, controlssignalslogic_1_eir,
       controlssignalslogic_1_embr, controlssignalslogic_1_epc, controlssignalslogic_1_f0,
       controlssignalslogic_1_f1, instructionsequencerfsm_1_execute, instructionsequencerfsm_1_t0,
       instructionsequencerfsm_1_t1, instructionsequencerfsm_1_t2, instructionsequencerfsm_1_t3,
       instructionsequencerfsm_1_t4, instructionsequencerfsm_1_t5, instructionsequencerfsm_1_t6,
       instructionsequencerfsm_1_t7, not_1_out, opcodedecoder_1_add, opcodedecoder_1_beq,
       opcodedecoder_1_bra, opcodedecoder_1_dec, opcodedecoder_1_inc, opcodedecoder_1_load,
       opcodedecoder_1_store, opcodedecoder_1_sub, ReadLocal, WriteLocal;
  wire [4:0] AdressBusLocal;

  InstructionSequencerFSM instructionsequencerfsm_1 (
    .Opcode(Opcode), .Clock(Clock), .T0(instructionsequencerfsm_1_t0), .T1(instructionsequencerfsm_1_t1),
    .T2(instructionsequencerfsm_1_t2), .T3(instructionsequencerfsm_1_t3), .T4(instructionsequencerfsm_1_t4),
    .T5(instructionsequencerfsm_1_t5), .T6(instructionsequencerfsm_1_t6), .T7(instructionsequencerfsm_1_t7),
    .Execute(instructionsequencerfsm_1_execute));
  OpcodeDecoder opcodedecoder_1 (
    .Opcode(Opcode), .Execute(instructionsequencerfsm_1_execute), .Load(opcodedecoder_1_load),
    .Store(opcodedecoder_1_store), .Add(opcodedecoder_1_add), .Sub(opcodedecoder_1_sub),
    .Inc(opcodedecoder_1_inc), .Dec(opcodedecoder_1_dec), .Bra(opcodedecoder_1_bra), .Beq(opcodedecoder_1_beq));
  and and_1 (and_1_out, WriteLocal, ~Clock);  // And
  ControlsSignalsLogic controlssignalslogic_1 (
    .Reset(Reset), .Clock(Clock), .Load(opcodedecoder_1_load), .Store(opcodedecoder_1_store),
    .Add(opcodedecoder_1_add), .Sub(opcodedecoder_1_sub), .Inc(opcodedecoder_1_inc),
    .Dec(opcodedecoder_1_dec), .Bra(opcodedecoder_1_bra), .Beq(opcodedecoder_1_beq),
    .T0(instructionsequencerfsm_1_t0), .T1(instructionsequencerfsm_1_t1), .T2(instructionsequencerfsm_1_t2),
    .T3(instructionsequencerfsm_1_t3), .T4(instructionsequencerfsm_1_t4), .T5(instructionsequencerfsm_1_t5),
    .T6(instructionsequencerfsm_1_t6), .T7(instructionsequencerfsm_1_t7), .Z(Z), .Read(ReadLocal),
    .Write(WriteLocal), .Cmar(controlssignalslogic_1_cmar), .Cmbr(controlssignalslogic_1_cmbr),
    .Embr(controlssignalslogic_1_embr), .Cir(controlssignalslogic_1_cir), .Eir(controlssignalslogic_1_eir),
    .Cpc(controlssignalslogic_1_cpc), .Epc(controlssignalslogic_1_epc), .Cd0(controlssignalslogic_1_cd0),
    .Ed0(controlssignalslogic_1_ed0), .Calu(controlssignalslogic_1_calu), .Ealu(controlssignalslogic_1_ealu),
    .F0(controlssignalslogic_1_f0), .F1(controlssignalslogic_1_f1));
  not not_1 (not_1_out, Reset);
  Seven_Seg_Hex seven_seg_hex_1 (.d({3'b000, AdressBusLocal[4]}), .dp(1'b0));
  EEPROM #(.AddrBits(5), .Bits(8)) ProgramDataMemory (
    .A(AdressBusLocal), .CS(not_1_out), .WE(and_1_out), .OE(ReadLocal), .D(DataBus));
  Seven_Seg_Hex seven_seg_hex_2 (.d(AdressBusLocal[3:0]), .dp(1'b0));
  Datapath datapath_1 (
    .Clock(Clock), .DataBus(DataBus), .Cmar(controlssignalslogic_1_cmar), .Cmbr(controlssignalslogic_1_cmbr),
    .Embr(controlssignalslogic_1_embr), .Cir(controlssignalslogic_1_cir), .Eir(controlssignalslogic_1_eir),
    .Cpc(controlssignalslogic_1_cpc), .Epc(controlssignalslogic_1_epc), .Cd0(controlssignalslogic_1_cd0),
    .Ed0(controlssignalslogic_1_ed0), .Calu(controlssignalslogic_1_calu), .Ealu(controlssignalslogic_1_ealu),
    .F0(controlssignalslogic_1_f0), .F1(controlssignalslogic_1_f1), .AddressBus(AddressBus), .Opcode(Opcode),
    .Z(Z));
  Seven_Seg_Hex seven_seg_hex_3 (.d(DataBus[7:4]), .dp(1'b0));
  Seven_Seg_Hex seven_seg_hex_4 (.d(DataBus[3:0]), .dp(1'b0));

  // Other names for the same wires on the sheet: AddressBusLocal[4:0] = AddressBus; ClockLocal = Clock;
  //   DataBusLocal[7:0] = DataBus; OpcodeLocal[2:0] = Opcode; ResetLocal = Reset; ZLocal = Z
endmodule
