// Digital circuit OpcodeDecoder-Inner.dig as structural Verilog
module OpcodeDecoder_Inner (
  input  [2:0] Opcode,
  input  Execute,
  output Load,
  output Store,
  output Add,
  output Sub,
  output Inc,
  output Dec,
  output Bra,
  output Beq
);

  wire not_1_out, not_2_out, not_3_out;

  not not_1 (not_1_out, Opcode[2]);
  not not_2 (not_2_out, Opcode[1]);
  not not_3 (not_3_out, Opcode[0]);
  and and_1 (Load, not_1_out, not_2_out, not_3_out, Execute);
  and and_2 (Store, not_1_out, not_2_out, Opcode[0], Execute);
  and and_3 (Add, not_1_out, Opcode[1], not_3_out, Execute);
  and and_4 (Sub, not_1_out, Opcode[1], Opcode[0], Execute);
  and and_5 (Inc, Opcode[2], not_2_out, not_3_out, Execute);
  and and_6 (Dec, Opcode[2], not_2_out, Opcode[0], Execute);
  and and_7 (Bra, Opcode[2], Opcode[1], not_3_out, Execute);
  and and_8 (Beq, Opcode[2], Opcode[1], Opcode[0], Execute);
endmodule
