// Digital circuit OpcodeDecoder.dig as structural Verilog
module OpcodeDecoder (
  input  [2:0] Opcode,
  input  Execute,
  output Load,
  output Store,
  output Add,
  output Sub,
  output Inc,
  output Dec,
  output Bra,
  output Beq
);

  OpcodeDecoder_Inner opcodedecoder_inner_1 (
    .Opcode(Opcode), .Execute(Execute), .Load(Load), .Store(Store), .Add(Add), .Sub(Sub), .Inc(Inc),
    .Dec(Dec), .Bra(Bra), .Beq(Beq));
endmodule

/* Test case Test Bench OpcodeDecoder-Inner:
# Test Vectors for opcode decoder
# Inputs: Opcode (3 bits), Execute
# Outputs: Load, Store, Add, Sub, Inc, Dec, Bra, Beq
# When Execute = 0, all outputs equal 0
# When execute = 1, decode Opcode
Opcode Execute Load Store Add Sub Inc Dec Bra Beq
# Load Instruction
0      0       0    0     0   0   0   0   0   0
0      1       1    0     0   0   0   0   0   0
# Store Instruction
1      0       0    0     0   0   0   0   0   0
1      1       0    1     0   0   0   0   0   0
# Add Instruction
2      0       0    0     0   0   0   0   0   0
2      1       0    0     1   0   0   0   0   0
# Subtract Instruction
3      0       0    0     0   0   0   0   0   0
3      1       0    0     0   1   0   0   0   0
# Increment Instruction
4      0       0    0     0   0   0   0   0   0
4      1       0    0     0   0   1   0   0   0
# Decrement Instruction
5      0       0    0     0   0   0   0   0   0
5      1       0    0     0   0   0   1   0   0
# Branch Instruction
6      0       0    0     0   0   0   0   0   0
6      1       0    0     0   0   0   0   1   0
# Branch if equal to zero Instruction
7      0       0    0     0   0   0   0   0   0
7      1       0    0     0   0   0   0   0   1
*/
