// Digital circuit ControlSignalsLogic.dig as structural Verilog
module ControlSignalsLogic (
  input  Reset,
  input  Load,
  input  Store,
  input  Add,
  input  Sub,
  input  Inc,
  input  Dec,
  input  Bra,
  input  Beq,
  input  T0,
  input  T1,
  input  T2,
  input  T3,
  input  T4,
  input  T5,
  input  T6,
  input  T7,
  input  Z,
  input  Clock,
  output Read,
  output Write,
  output Cmar,
  output Cmbr,
  output Embr,
  output Cir,
  output Eir,
  output Cpc,
  output Epc,
  output Cd0,
  output Ed0,
  output Calu,
  output Ealu,
  output F1,
  output F0
);

  ControlSignalsLogic_Inner controlsignalslogic_inner_1 (
    .Reset(Reset), .Clock(Clock), .Load(Load), .Store(Store), .Add(Add), .Sub(Sub), .Inc(Inc), .Dec(Dec),
    .Bra(Bra), .Beq(Beq), .T0(T0), .T1(T1), .T2(T2), .T3(T3), .T4(T4), .T5(T5), .T6(T6), .T7(T7), .Z(Z),
    .Read(Read), .Write(Write), .Cmar(Cmar), .Cmbr(Cmbr), .Embr(Embr), .Cir(Cir), .Eir(Eir), .Cpc(Cpc),
    .Epc(Epc), .Cd0(Cd0), .Ed0(Ed0), .Ealu(Ealu), .F0(F1), .F1(F0), .Calu(Calu));
endmodule

/* Test case:
# Test vectors for control signals logic
Reset Clock Load Store Add Sub Inc Dec Bra Beq T0 T1 T2 T3 T4 T5 T6 T7 Z Read Write Cmar Cmbr Cpc Cir Cd0 Calu Embr Epc Eir Ed0 Ealu F1 F0
# Fetch: MAR <- [PC]
0     1     0    0     0   0   0   0   0   0   1  0  0  0  0  0  0  0  0 0    0     1    0    0   0   0   0    0    1   0   0   0    0  0 
0     0     0    0     0   0   0   0   0   0   1  0  0  0  0  0  0  0  0 0    0     1    0    0   0   0   0    0    1   0   0   0    0  0 
# IR <- [MAR]
0     1     0    0     0   0   0   0   0   0   0  1  0  0  0  0  0  0  0 1    0     0    0    0   1   0   0    0    0   0   0   0    0  0 
0     0     0    0     0   0   0   0   0   0   0  1  0  0  0  0  0  0  0 1    0     0    0    0   1   0   0    0    0   0   0   0    0  0 
# ALU (Q) <- [PC]
0     1     0    0     0   0   0   0   0   0   0  0  1  0  0  0  0  0  0 0    0     0    0    0   0   0   1    0    1   0   0   0    1  0 
0     0     0    0     0   0   0   0   0   0   0  0  1  0  0  0  0  0  0 0    0     0    0    0   0   0   1    0    1   0   0   0    1  0 
# PC <- [ALU]
0     1     0    0     0   0   0   0   0   0   0  0  0  1  0  0  0  0  0 0    0     0    0    1   0   0   0    0    0   0   0   1    0  0 
0     0     0    0     0   0   0   0   0   0   0  0  0  1  0  0  0  0  0 0    0     0    0    1   0   0   0    0    0   0   0   1    0  0 
# Load: MAR <- [IR]
0     1     1    0     0   0   0   0   0   0   0  0  0  0  1  0  0  0  0 0    0     1    0    0   0   0   0    0    0   1   0   0    0  0 
0     0     1    0     0   0   0   0   0   0   0  0  0  0  1  0  0  0  0 0    0     1    0    0   0   0   0    0    0   1   0   0    0  0 
# D0 <- [MAR]
0     1     1    0     0   0   0   0   0   0   0  0  0  0  0  1  0  0  0 1    0     0    0    0   0   1   0    0    0   0   0   0    0  0 
0     0     1    0     0   0   0   0   0   0   0  0  0  0  0  1  0  0  0 1    0     0    0    0   0   1   0    0    0   0   0   0    0  0 
# Store: MAR <- [IR]
0     1     0    1     0   0   0   0   0   0   0  0  0  0  1  0  0  0  0 0    0     1    0    0   0   0   0    0    0   1   0   0    0  0 
0     0     0    1     0   0   0   0   0   0   0  0  0  0  1  0  0  0  0 0    0     1    0    0   0   0   0    0    0   1   0   0    0  0 
# [MAR] <- [D0]
0     1     0    1     0   0   0   0   0   0   0  0  0  0  0  1  0  0  0 0    1     0    0    0   0   0   0    0    0   0   1   0    0  0 
0     0     0    1     0   0   0   0   0   0   0  0  0  0  0  1  0  0  0 0    1     0    0    0   0   0   0    0    0   0   1   0    0  0 
#eset Clock Load Store Add Sub Inc Dec Bra Beq T0 T1 T2 T3 T4 T5 T6 T7 Z Read Write Cmar Cmbr Cpc Cir Cd0 Calu Embr Epc Eir Ed0 Ealu F1 F0
# Add: MAR <- [IR]
0     1     0    0     1   0   0   0   0   0   0  0  0  0  1  0  0  0  0 0    0     1    0    0   0   0   0    0    0   1   0   0    0  0 
0     0     0    0     1   0   0   0   0   0   0  0  0  0  1  0  0  0  0 0    0     1    0    0   0   0   0    0    0   1   0   0    0  0 
# MBR <- [MAR]
0     1     0    0     1   0   0   0   0   0   0  0  0  0  0  1  0  0  0 1    0     0    1    0   0   0   0    0    0   0   0   0    0  0 
0     0     0    0     1   0   0   0   0   0   0  0  0  0  0  1  0  0  0 1    0     0    1    0   0   0   0    0    0   0   0   0    0  0 
# ALU (P) <- [MBR]
0     1     0    0     1   0   0   0   0   0   0  0  0  0  0  0  1  0  0 0    0     0    0    0   0   0   1    1    0   0   0   0    0  0 
0     0     0    0     1   0   0   0   0   0   0  0  0  0  0  0  1  0  0 0    0     0    0    0   0   0   1    1    0   0   0   0    0  0 
# D0 <- [ALU}
0     1     0    0     1   0   0   0   0   0   0  0  0  0  0  0  0  1  0 0    0     0    0    0   0   1   0    0    0   0   0   1    0  0 
0     0     0    0     1   0   0   0   0   0   0  0  0  0  0  0  0  1  0 0    0     0    0    0   0   1   0    0    0   0   0   1    0  0 
# Sub: MAR <- [IR]
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*/
