// Digital circuit ClearLogic.dig as structural Verilog
module ClearLogic (
  input  [2:0] Opcode,
  input  T4,
  input  T5,
  output Clear
);

  wire and_1_out, and_2_out, and_3_out, and_4_out, and_5_out, and_6_out, and_7_out, and_8_out, not_1_out,
       not_2_out, not_3_out;

  not not_1 (not_1_out, Opcode[2]);
  not not_2 (not_2_out, Opcode[1]);
  not not_3 (not_3_out, Opcode[0]);
  and and_1 (and_1_out, not_1_out, not_2_out, not_3_out);
  and and_2 (and_2_out, Opcode[0], not_2_out, not_1_out);
  and and_3 (and_3_out, not_3_out, Opcode[1], Opcode[2]);
  and and_4 (and_4_out, Opcode[0], Opcode[1], Opcode[2]);
  and and_5 (and_5_out, T5, and_1_out);
  and and_6 (and_6_out, T5, and_2_out);
  and and_7 (and_7_out, and_3_out, T4);
  and and_8 (and_8_out, and_4_out, T4);
  or or_1 (Clear, and_5_out, and_6_out, and_7_out, and_8_out);

  // Other names for the same wires on the sheet: T4Local = T4; T5Local = T5

  // Notes on the sheet:
  //   Load
  //   Store
  //   Bra
  //   Beq
endmodule

/* Test case:
Opcode T4 T5 Clear
   0    0  0   0
   0    0  1   1
   0    1  0   0
   1    0  0   0
   1    0  1   1
   1    1  0   0
   2    0  0   0
   2    0  1   0
   2    1  0   0
   3    0  0   0
   3    0  1   0
   3    1  0   0
   4    0  0   0
   4    0  1   0
   4    1  0   0
   5    0  0   0
   5    0  1   0
   5    1  0   0
   6    0  0   0
   6    0  1   0
   6    1  0   1
   7    0  0   0
   7    0  1   0
   7    1  0   1
*/
