// Digital circuit InstructionSequencerFSM-Outer.dig as structural Verilog
module InstructionSequencerFSM_Outer (
  input  [2:0] Opcode,
  input  Clock,
  output T0,
  output T1,
  output T2,
  output T3,
  output T4,
  output T5,
  output T6,
  output T7,
  output Execute
);

  // InstructionSequencerFSM_Inner instructionsequencerfsm_inner_1: pin names not known; wires that end beside it: Opcode, Clock, T0, T1, T2, T3, T4, T5, T6, T7, Execute
endmodule

/* Test case:
Clock Opcode T0 T1 T2 T3 T4 T5 T6 T7 Execute
  0     0     1  0  0  0  0  0  0  0    0
  1     0     0  1  0  0  0  0  0  0    0
  0     0     0  1  0  0  0  0  0  0    0
  1     0     0  0  1  0  0  0  0  0    0
  0     0     0  0  1  0  0  0  0  0    0
  1     0     0  0  0  1  0  0  0  0    0
  0     0     0  0  0  1  0  0  0  0    0
  1     0     0  0  0  0  1  0  0  0    1
  0     0     0  0  0  0  1  0  0  0    1
  1     0     0  0  0  0  0  1  0  0    1
  0     0     0  0  0  0  0  1  0  0    1
#Clock Opcode T0 T1 T2 T3 T4 T5 T6 T7 Execute
  1     1     1  0  0  0  0  0  0  0    0
  0     1     1  0  0  0  0  0  0  0    0
  1     1     0  1  0  0  0  0  0  0    0
  0     1     0  1  0  0  0  0  0  0    0
  1     1     0  0  1  0  0  0  0  0    0
  0     1     0  0  1  0  0  0  0  0    0
  1     1     0  0  0  1  0  0  0  0    0
  0     1     0  0  0  1  0  0  0  0    0
  1     1     0  0  0  0  1  0  0  0    1
  0     1     0  0  0  0  1  0  0  0    1
  1     1     0  0  0  0  0  1  0  0    1
  0     1     0  0  0  0  0  1  0  0    1
#Clock Opcode T0 T1 T2 T3 T4 T5 T6 T7 Execute
  1     2     1  0  0  0  0  0  0  0    0
  0     2     1  0  0  0  0  0  0  0    0
  1     2     0  1  0  0  0  0  0  0    0
  0     2     0  1  0  0  0  0  0  0    0
  1     2     0  0  1  0  0  0  0  0    0
  0     2     0  0  1  0  0  0  0  0    0
  1     2     0  0  0  1  0  0  0  0    0
  0     2     0  0  0  1  0  0  0  0    0
  1     2     0  0  0  0  1  0  0  0    1
  0     2     0  0  0  0  1  0  0  0    1
  1     2     0  0  0  0  0  1  0  0    1
  0     2     0  0  0  0  0  1  0  0    1
  1     2     0  0  0  0  0  0  1  0    1
  0     2     0  0  0  0  0  0  1  0    1
  1     2     0  0  0  0  0  0  0  1    1
  0     2     0  0  0  0  0  0  0  1    1
#Clock Opcode T0 T1 T2 T3 T4 T5 T6 T7 Execute
  1     3     1  0  0  0  0  0  0  0    0
  0     3     1  0  0  0  0  0  0  0    0
  1     3     0  1  0  0  0  0  0  0    0
  0     3     0  1  0  0  0  0  0  0    0
  1     3     0  0  1  0  0  0  0  0    0
  0     3     0  0  1  0  0  0  0  0    0
  1     3     0  0  0  1  0  0  0  0    0
  0     3     0  0  0  1  0  0  0  0    0
  1     3     0  0  0  0  1  0  0  0    1
  0     3     0  0  0  0  1  0  0  0    1
  1     3     0  0  0  0  0  1  0  0    1
  0     3     0  0  0  0  0  1  0  0    1
  1     3     0  0  0  0  0  0  1  0    1
  0     3     0  0  0  0  0  0  1  0    1
  1     3     0  0  0  0  0  0  0  1    1
  0     3     0  0  0  0  0  0  0  1    1
#Clock Opcode T0 T1 T2 T3 T4 T5 T6 T7 Execute
  1     4     1  0  0  0  0  0  0  0    0
  0     4     1  0  0  0  0  0  0  0    0
  1     4     0  1  0  0  0  0  0  0    0
  0     4     0  1  0  0  0  0  0  0    0
  1     4     0  0  1  0  0  0  0  0    0
  0     4     0  0  1  0  0  0  0  0    0
  1     4     0  0  0  1  0  0  0  0    0
  0     4     0  0  0  1  0  0  0  0    0
  1     4     0  0  0  0  1  0  0  0    1
  0     4     0  0  0  0  1  0  0  0    1
  1     4     0  0  0  0  0  1  0  0    1
  0     4     0  0  0  0  0  1  0  0    1
  1     4     0  0  0  0  0  0  1  0    1
  0     4     0  0  0  0  0  0  1  0    1
  1     4     0  0  0  0  0  0  0  1    1
  0     4     0  0  0  0  0  0  0  1    1
#Clock Opcode T0 T1 T2 T3 T4 T5 T6 T7 Execute
  1     5     1  0  0  0  0  0  0  0    0
  0     5     1  0  0  0  0  0  0  0    0
  1     5     0  1  0  0  0  0  0  0    0
  0     5     0  1  0  0  0  0  0  0    0
  1     5     0  0  1  0  0  0  0  0    0
  0     5     0  0  1  0  0  0  0  0    0
  1     5     0  0  0  1  0  0  0  0    0
  0     5     0  0  0  1  0  0  0  0    0
  1     5     0  0  0  0  1  0  0  0    1
  0     5     0  0  0  0  1  0  0  0    1
  1     5     0  0  0  0  0  1  0  0    1
  0     5     0  0  0  0  0  1  0  0    1
  1     5     0  0  0  0  0  0  1  0    1
  0     5     0  0  0  0  0  0  1  0    1
  1     5     0  0  0  0  0  0  0  1    1
  0     5     0  0  0  0  0  0  0  1    1
#Clock Opcode T0 T1 T2 T3 T4 T5 T6 T7 Execute
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*/
