// Digital circuit Simple CPU.dig as structural Verilog
module Simple_CPU (
  input  Clock,
  input  Reset,
  output [7:0] DataBus,
  output [4:0] AddressBus,
  output [2:0] Opcode,
  output Z
);

  wire and_1_out, controlsignalsdesign_1_calu, controlsignalsdesign_1_cd0, controlsignalsdesign_1_cir,
       controlsignalsdesign_1_cmar, controlsignalsdesign_1_cmbr, controlsignalsdesign_1_cpc,
       controlsignalsdesign_1_ealu, controlsignalsdesign_1_ed0, controlsignalsdesign_1_eir,
       controlsignalsdesign_1_embr, controlsignalsdesign_1_epc, controlsignalsdesign_1_f0,
       controlsignalsdesign_1_f1, instructionsequencerfsm_1_execute, instructionsequencerfsm_1_t0,
       instructionsequencerfsm_1_t1, instructionsequencerfsm_1_t2, instructionsequencerfsm_1_t3,
       instructionsequencerfsm_1_t4, instructionsequencerfsm_1_t5, instructionsequencerfsm_1_t6,
       instructionsequencerfsm_1_t7, not_1_out, opcodedecoder_1_add, opcodedecoder_1_beq,
       opcodedecoder_1_bra, opcodedecoder_1_dec, opcodedecoder_1_inc, opcodedecoder_1_load,
       opcodedecoder_1_store, opcodedecoder_1_sub, ReadLocal, WriteLocal;

  InstructionSequencerFSM instructionsequencerfsm_1 (
    .Opcode(Opcode), .Clock(Clock), .T0(instructionsequencerfsm_1_t0), .T1(instructionsequencerfsm_1_t1),
    .T2(instructionsequencerfsm_1_t2), .T3(instructionsequencerfsm_1_t3), .T4(instructionsequencerfsm_1_t4),
    .T5(instructionsequencerfsm_1_t5), .T6(instructionsequencerfsm_1_t6), .T7(instructionsequencerfsm_1_t7),
    .Execute(instructionsequencerfsm_1_execute));
  OpcodeDecoder opcodedecoder_1 (
    .Opcode(Opcode), .Execute(instructionsequencerfsm_1_execute), .Load(opcodedecoder_1_load),
    .Store(opcodedecoder_1_store), .Add(opcodedecoder_1_add), .Sub(opcodedecoder_1_sub),
    .Inc(opcodedecoder_1_inc), .Dec(opcodedecoder_1_dec), .Bra(opcodedecoder_1_bra), .Beq(opcodedecoder_1_beq));
  and and_1 (and_1_out, WriteLocal, ~Clock);  // And
  ControlSignalsDesign controlsignalsdesign_1 (
    .Reset(Reset), .Clock(Clock), .Load(opcodedecoder_1_load), .Store(opcodedecoder_1_store),
    .Add(opcodedecoder_1_add), .Sub(opcodedecoder_1_sub), .Inc(opcodedecoder_1_inc),
    .Dec(opcodedecoder_1_dec), .Bra(opcodedecoder_1_bra), .Beq(opcodedecoder_1_beq),
    .T0(instructionsequencerfsm_1_t0), .T1(instructionsequencerfsm_1_t1), .T2(instructionsequencerfsm_1_t2),
    .T3(instructionsequencerfsm_1_t3), .T4(instructionsequencerfsm_1_t4), .T5(instructionsequencerfsm_1_t5),
    .T6(instructionsequencerfsm_1_t6), .T7(instructionsequencerfsm_1_t7), .Z(Z), .Read(ReadLocal),
    .Write(WriteLocal), .Cmar(controlsignalsdesign_1_cmar), .Cmbr(controlsignalsdesign_1_cmbr),
    .Embr(controlsignalsdesign_1_embr), .Cir(controlsignalsdesign_1_cir), .Eir(controlsignalsdesign_1_eir),
    .Cpc(controlsignalsdesign_1_cpc), .Epc(controlsignalsdesign_1_epc), .Cd0(controlsignalsdesign_1_cd0),
    .Ed0(controlsignalsdesign_1_ed0), .Calu(controlsignalsdesign_1_calu), .Ealu(controlsignalsdesign_1_ealu),
    .F0(controlsignalsdesign_1_f0), .F1(controlsignalsdesign_1_f1));
  not not_1 (not_1_out, Reset);
  Seven_Seg_Hex seven_seg_hex_1 (.d({3'b000, AddressBus[4]}), .dp(1'b0));
  EEPROM #(.AddrBits(5), .Bits(8)) ProgramDataMemory (
    .A(AddressBus), .CS(not_1_out), .WE(and_1_out), .OE(ReadLocal), .D(DataBus));
  Seven_Seg_Hex seven_seg_hex_2 (.d(AddressBus[3:0]), .dp(1'b0));
  Datapath datapath_1 (
    .Clock(Clock), .DataBus(DataBus), .Cmar(controlsignalsdesign_1_cmar), .Cmbr(controlsignalsdesign_1_cmbr),
    .Embr(controlsignalsdesign_1_embr), .Cir(controlsignalsdesign_1_cir), .Eir(controlsignalsdesign_1_eir),
    .Cpc(controlsignalsdesign_1_cpc), .Epc(controlsignalsdesign_1_epc), .Cd0(controlsignalsdesign_1_cd0),
    .Ed0(controlsignalsdesign_1_ed0), .Calu(controlsignalsdesign_1_calu), .Ealu(controlsignalsdesign_1_ealu),
    .F0(controlsignalsdesign_1_f0), .F1(controlsignalsdesign_1_f1), .AddressBus(AddressBus), .Opcode(Opcode),
    .Z(Z));
  Seven_Seg_Hex seven_seg_hex_3 (.d(DataBus[7:4]), .dp(1'b0));
  Seven_Seg_Hex seven_seg_hex_4 (.d(DataBus[3:0]), .dp(1'b0));

  // Other names for the same wires on the sheet: AddressBusLocal[4:0] = AddressBus; ClockLocal = Clock;
  //   DataBusLocal[7:0] = DataBus; OpcodeLocal[2:0] = Opcode; ResetLocal = Reset; ZLocal = Z

  // Notes on the sheet:
  //   contents of ProgramDataMemory (hex, n*v repeats v):
  //   19,53,33,16*0,b9,5*0,6
endmodule

/* Test case:
Reset Clock AddressBus DataBus  MAR  MBR  IR  PC  D0 Opcode Z
  0     0       0         0      0    0    0   0   0    0   1
  0     1       0         25     0    0    0   0   0    0   0
  0     0       0         25     0    0    0   0   0    0   0
  0     1       0         0      0    0    25  0   0    0   0
  0     0       0         0      0    0    25  0   0    0   0
  0     1       0         1      0    0    25  0   0    0   0
  0     0       0         1      0    0    25  0   0    0   0
  0     1       0         25     0    0    25  1   0    0   0
  0     0       0         25     0    0    25  1   0    0   0
  0     1       25        6      25   0    25  1   0    0   0
  0     0       25        6      25   0    25  1   0    0   0
  0     1       25        1      25   0    25  1   6    0   0
  0     0       25        1      25   0    25  1   6    0   0
  0     1       1         83     1    0    25  1   6    0   0
  0     0       1         83     1    0    25  1   6    0   0
  0     1       1         1      1    0    83  1   6    2   0
  0     0       1         1      1    0    83  1   6    2   0
  0     1       1         2      1    0    83  1   6    2   0
  0     0       1         2      1    0    83  1   6    2   0
  0     1       1         83     1    0    83  2   6    2   0
  0     0       1         83     1    0    83  2   6    2   0
  0     1       19        185    83   0    83  2   6    2   0
  0     0       19        185    83   0    83  2   6    2   0
  0     1       19        185    83   185  83  2   6    2   0
  0     0       19        185    83   185  83  2   6    2   0
  0     1       19        191    83   185  83  2   6    2   0
  0     0       19        191    83   185  83  2   6    2   0
  0     1       19        2      83   185  83  2   191  2   0
  0     0       19        2      83   185  83  2   191  2   0
  0     1       2         51     2    185  83  2   191  2   0
  0     0       2         51     2    185  83  2   191  2   0
  0     1       2         2      2    185  51  2   191  1   0
  0     0       2         2      2    185  51  2   191  1   0
  0     1       2         3      2    185  51  2   191  1   0
  0     0       2         3      2    185  51  2   191  1   0
  0     1       2         51     2    185  51  3   191  1   0
  0     0       2         51     2    185  51  3   191  1   0
  0     1       19        191    51   185  51  3   191  1   0
  0     0       19        191    51   185  51  3   191  1   0
  0     1       19        3      51   185  51  3   191  1   0
  0     0       19        3      51   185  51  3   191  1   0
*/
