// Digital circuit ALU.dig as structural Verilog
module ALU (
  input  [7:0] PIn,
  input  [7:0] DataBus,
  input  F0,
  input  F1,
  output [7:0] ALUOut,
  output Z
);

  wire Add, Bit_0_cout, Bit_1_cout, Bit_2_cout, Bit_3_cout, Bit_4_cout, Bit_5_cout, Bit_6_cout, Dec, Inc,
       multiplexer_1_out, multiplexer_2_out, multiplexer_3_out, multiplexer_4_out, multiplexer_5_out,
       multiplexer_6_out, multiplexer_7_out, multiplexer_8_out, or_1_out, Sub, xor_1_out, xor_2_out,
       xor_3_out, xor_4_out, xor_5_out, xor_6_out, xor_7_out, xor_8_out;

  Decoder #(.Selector_Bits(2)) decoder_1 (.sel({F1, F0}), .out_0(Add), .out_1(Sub), .out_2(Inc), .out_3(Dec));
  or or_1 (or_1_out, Sub, Inc);
  xor xor_1 (xor_1_out, Sub, DataBus[7]);
  xor xor_2 (xor_2_out, Sub, DataBus[6]);
  xor xor_3 (xor_3_out, Sub, DataBus[5]);
  xor xor_4 (xor_4_out, Sub, DataBus[4]);
  xor xor_5 (xor_5_out, Sub, DataBus[3]);
  xor xor_6 (xor_6_out, Sub, DataBus[2]);
  xor xor_7 (xor_7_out, Sub, DataBus[1]);
  xor xor_8 (xor_8_out, Sub, DataBus[0]);
  Multiplexer multiplexer_1 (.sel(F1), .in_0(PIn[7]), .in_1(F0), .out(multiplexer_1_out));
  Multiplexer multiplexer_2 (.sel(F1), .in_0(PIn[6]), .in_1(F0), .out(multiplexer_2_out));
  Multiplexer multiplexer_3 (.sel(F1), .in_0(PIn[5]), .in_1(F0), .out(multiplexer_3_out));
  Multiplexer multiplexer_4 (.sel(F1), .in_0(PIn[4]), .in_1(F0), .out(multiplexer_4_out));
  Multiplexer multiplexer_5 (.sel(F1), .in_0(PIn[3]), .in_1(F0), .out(multiplexer_5_out));
  Multiplexer multiplexer_6 (.sel(F1), .in_0(PIn[2]), .in_1(F0), .out(multiplexer_6_out));
  Multiplexer multiplexer_7 (.sel(F1), .in_0(PIn[1]), .in_1(F0), .out(multiplexer_7_out));
  Multiplexer multiplexer_8 (.sel(F1), .in_0(PIn[0]), .in_1(F0), .out(multiplexer_8_out));
  FullAdder Bit_7 (.A(multiplexer_1_out), .B(xor_1_out), .Cin(Bit_6_cout), .S(ALUOut[7]));  // open: Cout
  FullAdder Bit_6 (.A(multiplexer_2_out), .B(xor_2_out), .Cin(Bit_5_cout), .Cout(Bit_6_cout), .S(ALUOut[6]));
  FullAdder Bit_5 (.A(multiplexer_3_out), .B(xor_3_out), .Cin(Bit_4_cout), .Cout(Bit_5_cout), .S(ALUOut[5]));
  FullAdder Bit_4 (.A(multiplexer_4_out), .B(xor_4_out), .Cin(Bit_3_cout), .Cout(Bit_4_cout), .S(ALUOut[4]));
  FullAdder Bit_3 (.A(multiplexer_5_out), .B(xor_5_out), .Cin(Bit_2_cout), .Cout(Bit_3_cout), .S(ALUOut[3]));
  FullAdder Bit_2 (.A(multiplexer_6_out), .B(xor_6_out), .Cin(Bit_1_cout), .Cout(Bit_2_cout), .S(ALUOut[2]));
  FullAdder Bit_1 (.A(multiplexer_7_out), .B(xor_7_out), .Cin(Bit_0_cout), .Cout(Bit_1_cout), .S(ALUOut[1]));
  FullAdder Bit_0 (.A(multiplexer_8_out), .B(xor_8_out), .Cin(or_1_out), .Cout(Bit_0_cout), .S(ALUOut[0]));
  nor nor_1 (Z, ALUOut[7], ALUOut[6], ALUOut[5], ALUOut[4], ALUOut[3], ALUOut[2], ALUOut[1], ALUOut[0]);

  // Other names for the same wires on the sheet: F0Local = F0; F1Local = F1; P0 = PIn[0]; P1 = PIn[1]; P2 = PIn[2];
  //   P3 = PIn[3]; P4 = PIn[4]; P5 = PIn[5]; P6 = PIn[6]; P7 = PIn[7]
endmodule

/* Test case:
F1 F0 PIn DataBus ALUOut
loop(i,128)
  let a = random(1<<8);
  let b = random(1<<8);
0  0  (a)   (b)   (a+b)
end loop
loop(i,128)
  let a = random(1<<8);
  let b = random(1<<8);
0  1  (a)   (b)   (a-b)
end loop
loop(i,128)
  let a = random(1<<8);
  let b = random(1<<8);
1  0  (a)   (b)   (b+1)
end loop
loop(i,128)
  let a = random(1<<8);
  let b = random(1<<8);
1  1  (a)   (b)   (b-1)
end loop
*/
