// Digital circuit AddressDecoder.dig as structural Verilog
module AddressDecoder (
  input  [4:0] AddressBus,
  output CS0,
  output CS1
);

  and and_1 (CS0, AddressBus[4], AddressBus[3], AddressBus[2], AddressBus[1], AddressBus[0]);
  not not_1 (CS1, CS0);
endmodule
