// Digital circuit ControlSignalsDesign.dig as structural Verilog
module ControlSignalsDesign (
  input  Reset,
  input  Clock,
  input  Load,
  input  Store,
  input  Add,
  input  Sub,
  input  Inc,
  input  Dec,
  input  Bra,
  input  Beq,
  input  T0,
  input  T1,
  input  T2,
  input  T3,
  input  T4,
  input  T5,
  input  T6,
  input  T7,
  input  Z,
  output Read,
  output Write,
  output Cmar,
  output Cmbr,
  output Embr,
  output Cir,
  output Eir,
  output Cpc,
  output Epc,
  output Cd0,
  output Ed0,
  output Calu,
  output Ealu,
  output F0,
  output F1
);

  wire and_1_out, and_2_out, and_3_out, and_4_out, and_5_out, and_6_out, and_7_out, and_8_out, and_9_out,
       and_10_out, and_11_out, and_12_out, and_13_out, and_14_out, and_15_out, and_16_out, and_17_out,
       and_18_out, and_19_out, and_20_out, and_21_out, and_22_out, and_23_out, and_25_out, and_26_out,
       and_27_out, and_28_out, and_29_out, and_30_out, and_31_out, and_32_out, and_33_out, and_34_out,
       and_35_out, and_36_out, and_37_out, and_38_out, and_39_out, and_40_out, and_41_out, and_42_out,
       and_43_out, and_44_out, and_45_out, and_46_out, and_47_out, and_48_out, multiplexer_1_out, not_1_out,
       ZStored;

  Multiplexer multiplexer_1 (.sel(T6), .in_0(ZStored), .in_1(Z), .out(multiplexer_1_out));
  not not_1 (not_1_out, Clock);
  D_FF d_ff_1 (.D(multiplexer_1_out), .C(not_1_out), .Q(ZStored));  // open: nQ
  and and_1 (and_1_out, T5, Load);
  and and_2 (and_2_out, T5, Add);
  and and_3 (and_3_out, T5, Sub);
  and and_4 (and_4_out, T5, Inc);
  and and_5 (and_5_out, T5, Dec);
  and and_6 (and_6_out, T5, Store);
  and and_7 (and_7_out, T7, Inc);
  and and_8 (and_8_out, T7, Dec);
  and and_9 (and_9_out, T4, Load);
  and and_10 (and_10_out, T4, Store);
  and and_11 (and_11_out, T4, Add);
  and and_12 (and_12_out, T4, Sub);
  and and_13 (and_13_out, T4, Inc);
  and and_14 (and_14_out, T4, Dec);
  or or_1 (Read, T1, and_1_out, and_2_out, and_3_out, and_4_out, and_5_out);
  or or_2 (Write, and_6_out, and_7_out, and_8_out);
  or or_3 (Cmar, T0, and_9_out, and_10_out, and_11_out, and_12_out, and_13_out, and_14_out);
  and and_15 (and_15_out, T5, Add);
  and and_16 (and_16_out, T5, Sub);
  and and_17 (and_17_out, T5, Inc);
  and and_18 (and_18_out, T5, Dec);
  and and_19 (and_19_out, T4, Bra);
  and and_20 (and_20_out, T4, ZStored, Beq);
  and and_21 (and_21_out, T5, Load);
  and and_22 (and_22_out, T7, Add);
  and and_23 (and_23_out, T7, Sub);
  and and_24 (Ed0, T5, Store);
  or or_4 (Cmbr, and_15_out, and_16_out, and_17_out, and_18_out);
  or or_5 (Cpc, T3, and_19_out, and_20_out);
  or or_6 (Cd0, and_21_out, and_22_out, and_23_out);
  and and_25 (and_25_out, T7, Add);
  and and_26 (and_26_out, T7, Sub);
  and and_27 (and_27_out, T7, Inc);
  and and_28 (and_28_out, T7, Dec);
  and and_29 (and_29_out, T6, Inc);
  and and_30 (and_30_out, T6, Dec);
  and and_31 (and_31_out, T6, Sub);
  and and_32 (and_32_out, T6, Dec);
  and and_33 (and_33_out, T6, Add);
  and and_34 (and_34_out, T6, Sub);
  and and_35 (and_35_out, T6, Inc);
  and and_36 (and_36_out, T6, Dec);
  or or_7 (Ealu, T3, and_25_out, and_26_out, and_27_out, and_28_out);
  or or_8 (F1, T2, and_29_out, and_30_out);
  or or_9 (F0, and_31_out, and_32_out);
  or or_10 (Calu, T2, and_33_out, and_34_out, and_35_out, and_36_out);
  and and_37 (and_37_out, T6, Add);
  and and_38 (and_38_out, T6, Sub);
  and and_39 (and_39_out, T6, Inc);
  and and_40 (and_40_out, T6, Dec);
  and and_41 (and_41_out, T4, Bra);
  and and_42 (and_42_out, T4, Load);
  and and_43 (and_43_out, T4, Store);
  and and_44 (and_44_out, T4, Add);
  and and_45 (and_45_out, T4, Sub);
  and and_46 (and_46_out, T4, Inc);
  and and_47 (and_47_out, T4, Dec);
  and and_48 (and_48_out, T4, ZStored, Beq);
  or or_11 (Embr, and_37_out, and_38_out, and_39_out, and_40_out);
  or or_12 (Epc, T0, T2);
  or or_13 (Eir, and_41_out, and_42_out, and_43_out, and_44_out, and_45_out, and_46_out, and_47_out, and_48_out);

  assign Cir = T1;

  // Other names for the same wires on the sheet: AddLocal = Add; BeqLocal = Beq; BraLocal = Bra; ClockLocal = Clock;
  //   DecLocal = Dec; IncLocal = Inc; LoadLocal = Load; ResetLocal = Reset; StoreLocal = Store; SubLocal = Sub;
  //   T0Local = T0; T1Local = T1; T2Local = T2; T3Local = T3; T4Local = T4; T5Local = T5; T6Local = T6; T7Local = T7;
  //   ZLocal = Z
endmodule

/* Test case:
# Test Vectors for Control Signals Logic
Reset Clock Load Store Add Sub Inc Dec Bra Beq T0 T1 T2 T3 T4 T5 T6 T7 Z Read Write Cmar Cmbr Cpc Cir Cd0 Calu Embr Epc Eir Ed0 Ealu F1 F0
# Fetch: MAR <- [PC]
0       1     0    0    0   0   0   0   0   0   1  0  0  0  0  0  0  0 0   0    0     1    0    0   0   0   0    0   1   0    0    0   0  0
0       0     0    0    0   0   0   0   0   0   1  0  0  0  0  0  0  0 0   0    0     1    0    0   0   0   0    0   1   0    0    0   0  0
# IR <- [MAR]
0       1     0    0    0   0   0   0   0   0   0  1  0  0  0  0  0  0 0   1    0     0    0    0   1   0   0    0   0   0    0    0   0  0
0       0     0    0    0   0   0   0   0   0   0  1  0  0  0  0  0  0 0   1    0     0    0    0   1   0   0    0   0   0    0    0   0  0
# ALU(Q) <- [PC]
0       1     0    0    0   0   0   0   0   0   0  0  1  0  0  0  0  0 0   0    0     0    0    0   0   0   1    0   1   0    0    0   1  0
0       0     0    0    0   0   0   0   0   0   0  0  1  0  0  0  0  0 0   0    0     0    0    0   0   0   1    0   1   0    0    0   1  0
# PC <- [ALU]
0       1     0    0    0   0   0   0   0   0   0  0  0  1  0  0  0  0 0   0    0     0    0    1   0   0   0    0   0   0    0    1   0  0
0       0     0    0    0   0   0   0   0   0   0  0  0  1  0  0  0  0 0   0    0     0    0    1   0   0   0    0   0   0    0    1   0  0
# Load
0       1     1    0    0   0   0   0   0   0   0  0  0  0  1  0  0  0 0   0    0     1    0    0   0   0   0    0   0   1    0    0   0  0
0       0     1    0    0   0   0   0   0   0   0  0  0  0  1  0  0  0 0   0    0     1    0    0   0   0   0    0   0   1    0    0   0  0
0       1     1    0    0   0   0   0   0   0   0  0  0  0  0  1  0  0 0   1    0     0    0    0   0   1   0    0   0   0    0    0   0  0
0       0     1    0    0   0   0   0   0   0   0  0  0  0  0  1  0  0 0   1    0     0    0    0   0   1   0    0   0   0    0    0   0  0
# Store
0       1     0    1    0   0   0   0   0   0   0  0  0  0  1  0  0  0 0   0    0     1    0    0   0   0   0    0   0   1    0    0   0  0
0       0     0    1    0   0   0   0   0   0   0  0  0  0  1  0  0  0 0   0    0     1    0    0   0   0   0    0   0   1    0    0   0  0
0       1     0    1    0   0   0   0   0   0   0  0  0  0  0  1  0  0 0   0    1     0    0    0   0   0   0    0   0   0    1    0   0  0
0       0     0    1    0   0   0   0   0   0   0  0  0  0  0  1  0  0 0   0    1     0    0    0   0   0   0    0   0   0    1    0   0  0
# Add
0       1     0    0    1   0   0   0   0   0   0  0  0  0  1  0  0  0 0   0    0     1    0    0   0   0   0    0   0   1    0    0   0  0
0       0     0    0    1   0   0   0   0   0   0  0  0  0  1  0  0  0 0   0    0     1    0    0   0   0   0    0   0   1    0    0   0  0
0       1     0    0    1   0   0   0   0   0   0  0  0  0  0  1  0  0 0   1    0     0    1    0   0   0   0    0   0   0    0    0   0  0
0       0     0    0    1   0   0   0   0   0   0  0  0  0  0  1  0  0 0   1    0     0    1    0   0   0   0    0   0   0    0    0   0  0
0       1     0    0    1   0   0   0   0   0   0  0  0  0  0  0  1  0 0   0    0     0    0    0   0   0   1    1   0   0    0    0   0  0
0       0     0    0    1   0   0   0   0   0   0  0  0  0  0  0  1  0 0   0    0     0    0    0   0   0   1    1   0   0    0    0   0  0
0       1     0    0    1   0   0   0   0   0   0  0  0  0  0  0  0  1 0   0    0     0    0    0   0   1   0    0   0   0    0    1   0  0
0       0     0    0    1   0   0   0   0   0   0  0  0  0  0  0  0  1 0   0    0     0    0    0   0   1   0    0   0   0    0    1   0  0
# Sub
0       1     0    0    0   1   0   0   0   0   0  0  0  0  1  0  0  0 0   0    0     1    0    0   0   0   0    0   0   1    0    0   0  0
0       0     0    0    0   1   0   0   0   0   0  0  0  0  1  0  0  0 0   0    0     1    0    0   0   0   0    0   0   1    0    0   0  0
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*/
