// Digital circuit Datapath.dig as structural Verilog
module Datapath (
  input  Clock,
  input  [7:0] DataBus,
  input  Cmar,
  input  Cmbr,
  input  Embr,
  input  Cir,
  input  Eir,
  input  Cpc,
  input  Epc,
  input  Cd0,
  input  Ed0,
  input  Calu,
  input  Ealu,
  input  F0,
  input  F1,
  output [4:0] AddressBus,
  output [2:0] Opcode,
  output Z
);

  wire [4:0] IR_dataout;
  wire [7:0] ALU_2_dataout, ALU_aluout, D0_dataout, MBR_dataout, PC_dataout;
  wire [7:5] MAR_dataout;

  Register MAR (.DataIn(DataBus), .ENIn(Cmar), .Clock(Clock), .DataOut({MAR_dataout, AddressBus}));
  Register MBR (.DataIn(DataBus), .ENIn(Cmbr), .Clock(Clock), .DataOut(MBR_dataout));
  Register IR (.DataIn(DataBus), .ENIn(Cir), .Clock(Clock), .DataOut({Opcode, IR_dataout}));
  Register PC (.DataIn(DataBus), .ENIn(Cpc), .Clock(Clock), .DataOut(PC_dataout));
  Register D0 (.DataIn(DataBus), .ENIn(Cd0), .Clock(Clock), .DataOut(D0_dataout));
  ALU ALU (.PIn(D0_dataout), .DataBus(DataBus), .F0(F0), .F1(F1), .ALUOut(ALU_aluout), .Z(Z));
  // Probe MBR on MBR_dataout
  // Probe PC on PC_dataout
  Register ALU_2 (.DataIn(ALU_aluout), .ENIn(Calu), .Clock(Clock), .DataOut(ALU_2_dataout));
  assign DataBus = Embr ? MBR_dataout : 8'bz;  // Driver driver_1
  assign DataBus = Eir ? {Opcode, IR_dataout} : 8'bz;  // Driver driver_2
  assign DataBus = Epc ? PC_dataout : 8'bz;  // Driver driver_3
  assign DataBus = Ed0 ? D0_dataout : 8'bz;  // Driver driver_4
  // Probe MAR on {MAR_dataout, AddressBus}
  // Probe IR on {Opcode, IR_dataout}
  // Probe D0 on D0_dataout
  assign DataBus = Ealu ? ALU_2_dataout : 8'bz;  // Driver driver_5
endmodule
