// Digital circuit FullAdder.dig as structural Verilog
module FullAdder (
  input  A,
  input  B,
  input  Cin,
  output Cout,
  output S
);

  wire and_1_out, and_2_out, and_3_out, xor_1_out;

  xor xor_1 (xor_1_out, A, B);
  and and_1 (and_1_out, A, B);
  and and_2 (and_2_out, B, Cin);
  and and_3 (and_3_out, A, Cin);
  xor xor_2 (S, xor_1_out, Cin);
  or or_1 (Cout, and_1_out, and_2_out, and_3_out);
endmodule

/* Test case:
A  B   Cin   S   Cout
0  0    0    0    0
0  0    1    1    0
0  1    0    1    0
0  1    1    0    1
1  0    0    1    0
1  0    1    0    1
1  1    0    0    1
1  1    1    1    1
*/
