// Digital circuit OpcodeDecoder.dig as structural Verilog
module OpcodeDecoder (
  input  [2:0] Opcode,
  input  Execute,
  output Load,
  output Store,
  output Add,
  output Sub,
  output Inc,
  output Dec,
  output Bra,
  output Beq
);

  wire not_1_out, not_2_out, not_3_out;

  not not_1 (not_1_out, Opcode[2]);
  not not_2 (not_2_out, Opcode[1]);
  not not_3 (not_3_out, Opcode[0]);
  and and_1 (Load, not_1_out, not_2_out, not_3_out, Execute);
  and and_2 (Store, not_1_out, not_2_out, Opcode[0], Execute);
  and and_3 (Add, not_1_out, Opcode[1], not_3_out, Execute);
  and and_4 (Sub, not_1_out, Opcode[1], Opcode[0], Execute);
  and and_5 (Inc, Opcode[2], not_2_out, not_3_out, Execute);
  and and_6 (Dec, Opcode[2], not_2_out, Opcode[0], Execute);
  and and_7 (Bra, Opcode[2], Opcode[1], not_3_out, Execute);
  and and_8 (Beq, Opcode[2], Opcode[1], Opcode[0], Execute);
endmodule

/* Test case:
# Test Vectors for opcode decoder
# Inputs: Opcode (3 bits), Execute
# Outputs: Load, Store, Add, Sub, Inc, Dec, Bra, Beq
# When Execute = 0, all outputs equal 0
# When execute = 1, decode Opcode
Opcode Execute Load Store Add Sub Inc Dec Bra Beq
# Load Instruction
0      0       0    0     0   0   0   0   0   0
0      1       1    0     0   0   0   0   0   0
# Store Instruction
1      0       0    0     0   0   0   0   0   0
1      1       0    1     0   0   0   0   0   0
# Add Instruction
2      0       0    0     0   0   0   0   0   0
2      1       0    0     1   0   0   0   0   0
# Subtract Instruction
3      0       0    0     0   0   0   0   0   0
3      1       0    0     0   1   0   0   0   0
# Increment Instruction
4      0       0    0     0   0   0   0   0   0
4      1       0    0     0   0   1   0   0   0
# Decrement Instruction
5      0       0    0     0   0   0   0   0   0
5      1       0    0     0   0   0   1   0   0
# Branch Instruction
6      0       0    0     0   0   0   0   0   0
6      1       0    0     0   0   0   0   1   0
# Branch if equal to zero Instruction
7      0       0    0     0   0   0   0   0   0
7      1       0    0     0   0   0   0   0   1
*/
