// Digital circuit OutputLogic.dig as structural Verilog
module OutputLogic (
  input  Q2,
  input  Q2_2,
  input  Q1,
  input  Q1_2,
  input  Q0,
  input  Q0_2,
  output T0,
  output T1,
  output T2,
  output T3,
  output T4,
  output T5,
  output T6,
  output T7,
  output Execute
);

  and and_1 (T0, Q2_2, Q1_2, Q0_2);
  and and_2 (T1, Q2_2, Q1_2, Q0);
  and and_3 (T2, Q2_2, Q1, Q0_2);
  and and_4 (T3, Q2_2, Q1, Q0);
  and and_5 (T4, Q2, Q1_2, Q0_2);
  and and_6 (T5, Q2, Q1_2, Q0);
  and and_7 (T6, Q2, Q1, Q0_2);
  and and_8 (T7, Q2, Q1, Q0);
  or or_1 (Execute, T4, T5, T6, T7);

  // Other names for the same wires on the sheet: Q0_Local = Q0_2; Q0Local = Q0; Q1_Local = Q1_2; Q1Local = Q1;
  //   Q2_Local = Q2_2; Q2Local = Q2
endmodule

/* Test case:
Q2 Q2' Q1 Q1' Q0 Q0' T0 T1 T2 T3 T4 T5 T6 T7 Execute
 0  1   0  1   0  1   1  0  0  0  0  0  0  0    0
 0  1   0  1   1  0   0  1  0  0  0  0  0  0    0
 0  1   1  0   0  1   0  0  1  0  0  0  0  0    0
 0  1   1  0   1  0   0  0  0  1  0  0  0  0    0
 1  0   0  1   0  1   0  0  0  0  1  0  0  0    1
 1  0   0  1   1  0   0  0  0  0  0  1  0  0    1
 1  0   1  0   0  1   0  0  0  0  0  0  1  0    1
 1  0   1  0   1  0   0  0  0  0  0  0  0  1    1
*/
