// Digital circuit PortRegister.dig as structural Verilog
module PortRegister (
  input  Read,
  input  Write,
  input  CS,
  input  [7:0] DataBus,
  output [7:0] DataOut
);

  wire and_1_out;

  and and_1 (and_1_out, Read, CS);
  assign DataBus = and_1_out ? DataOut : 8'bz;  // Driver driver_1
  Register #(.Bits(8)) Register (.D(DataBus), .C(Write), .en(CS), .Q(DataOut));
endmodule
