// Digital circuit Register.dig as structural Verilog
module Register (
  input  [7:0] DataIn,
  input  ENIn,
  input  Clock,
  output [7:0] DataOut
);

  wire multiplexer_1_out, multiplexer_2_out, multiplexer_3_out, multiplexer_4_out, multiplexer_5_out,
       multiplexer_6_out, multiplexer_7_out, multiplexer_8_out;

  Multiplexer multiplexer_1 (.sel(ENIn), .in_0(DataOut[7]), .in_1(DataIn[7]), .out(multiplexer_1_out));
  Multiplexer multiplexer_2 (.sel(ENIn), .in_0(DataOut[6]), .in_1(DataIn[6]), .out(multiplexer_2_out));
  Multiplexer multiplexer_3 (.sel(ENIn), .in_0(DataOut[5]), .in_1(DataIn[5]), .out(multiplexer_3_out));
  Multiplexer multiplexer_4 (.sel(ENIn), .in_0(DataOut[4]), .in_1(DataIn[4]), .out(multiplexer_4_out));
  Multiplexer multiplexer_5 (.sel(ENIn), .in_0(DataOut[3]), .in_1(DataIn[3]), .out(multiplexer_5_out));
  Multiplexer multiplexer_6 (.sel(ENIn), .in_0(DataOut[2]), .in_1(DataIn[2]), .out(multiplexer_6_out));
  Multiplexer multiplexer_7 (.sel(ENIn), .in_0(DataOut[1]), .in_1(DataIn[1]), .out(multiplexer_7_out));
  Multiplexer multiplexer_8 (.sel(ENIn), .in_0(DataOut[0]), .in_1(DataIn[0]), .out(multiplexer_8_out));
  D_FF Q7 (.D(multiplexer_1_out), .C(Clock), .Q(DataOut[7]));  // open: nQ
  D_FF Q6 (.D(multiplexer_2_out), .C(Clock), .Q(DataOut[6]));  // open: nQ
  D_FF Q5 (.D(multiplexer_3_out), .C(Clock), .Q(DataOut[5]));  // open: nQ
  D_FF Q4 (.D(multiplexer_4_out), .C(Clock), .Q(DataOut[4]));  // open: nQ
  D_FF Q3 (.D(multiplexer_5_out), .C(Clock), .Q(DataOut[3]));  // open: nQ
  D_FF Q2 (.D(multiplexer_6_out), .C(Clock), .Q(DataOut[2]));  // open: nQ
  D_FF Q1 (.D(multiplexer_7_out), .C(Clock), .Q(DataOut[1]));  // open: nQ
  D_FF Q0 (.D(multiplexer_8_out), .C(Clock), .Q(DataOut[0]));  // open: nQ
endmodule
