// Digital circuit Simple Computer System.dig as structural Verilog
module Simple_Computer_System (
  input  Clock,
  input  Reset
);

  wire addressdecoder_1_cs0, addressdecoder_1_cs1, simple_cpu_1_read, simple_cpu_1_write;
  wire [4:0] simple_cpu_1_addressbus;
  wire [7:0] portregister_1_dataout, ProgramDataMemory_d;

  Simple_CPU simple_cpu_1 (
    .Clock(Clock), .Reset(Reset), .DataBus(ProgramDataMemory_d), .AddressBus(simple_cpu_1_addressbus),
    .Write(simple_cpu_1_write), .Read(simple_cpu_1_read));
  AddressDecoder addressdecoder_1 (
    .AddressBus(simple_cpu_1_addressbus), .CS0(addressdecoder_1_cs0), .CS1(addressdecoder_1_cs1));
  EEPROM #(.AddrBits(5), .Bits(8)) ProgramDataMemory (
    .A(simple_cpu_1_addressbus), .CS(addressdecoder_1_cs1), .WE(simple_cpu_1_write), .OE(simple_cpu_1_read),
    .D(ProgramDataMemory_d));
  PortRegister portregister_1 (
    .Read(simple_cpu_1_read), .Write(simple_cpu_1_write), .CS(addressdecoder_1_cs0),
    .DataBus(ProgramDataMemory_d), .DataOut(portregister_1_dataout));
  Seven_Seg_Hex seven_seg_hex_1 (.d(portregister_1_dataout[7:4]), .dp(1'b0));
  Seven_Seg_Hex seven_seg_hex_2 (.d(portregister_1_dataout[3:0]), .dp(1'b0));

  // Notes on the sheet:
  //   Clock: Hz: 100
  //   contents of ProgramDataMemory (hex, n*v repeats v):
  //   18,3f,9f,19,7f,e7,c2,bf,1f,5f,e0,c7,13*0,a
endmodule
